// Logisim project CPU2.circ as structural Verilog: 17 circuits, main circuit main
module main (
  input  [15:0] Val,
  input  [15:0] Addr,
  input  set,
  input  get,
  input  [7:0] Key_Address,
  input  RAM_set,
  input  [7:0] Key_Value
);

  wire clock_1_out, memory_mapper_1_ram_get_2, memory_mapper_1_ram_set_2, memory_mapper_1_screen_set;
  wire [9:0] memory_mapper_1_screen_address_out, memory_mapper_1_screen_value_out;
  wire [15:0] memory_mapper_1_ram_address_out, memory_mapper_1_ram_value_out, ram_1_data;

  Memory_Mapper memory_mapper_1 (
    .RAM_Value_In(Val), .RAM_Address_In(Addr), .RAM_set(set), .RAM_get(get),
    .Ram_Value_Out(memory_mapper_1_ram_value_out), .Ram_Address_Out(memory_mapper_1_ram_address_out),
    .RAM_set_2(memory_mapper_1_ram_set_2), .RAM_get_2(memory_mapper_1_ram_get_2), .Key_Value_In(Key_Value),
    .Key_Address_In(Key_Address), .Key_Set(RAM_set), .Screen_Value_Out(memory_mapper_1_screen_value_out),
    .Screen_Address_Out(memory_mapper_1_screen_address_out), .Screen_Set(memory_mapper_1_screen_set));
  Clock clock_1 (.out(clock_1_out));
  Hex_Digit_Display hex_digit_display_1 (.value(ram_1_data[3:0]));  // open: dp
  RAM #(.addrWidth(16), .dataWidth(16), .bus("separate")) ram_1 (
    .addr(memory_mapper_1_ram_address_out), .din(memory_mapper_1_ram_value_out), .data(ram_1_data),
    .str(memory_mapper_1_ram_set_2), .sel(1'b1), .clk(clock_1_out), .ld(memory_mapper_1_ram_get_2));  // open: clr
  Hex_Digit_Display hex_digit_display_2 (.value(ram_1_data[7:4]));  // open: dp
  Hex_Digit_Display hex_digit_display_3 (.value(ram_1_data[11:8]));  // open: dp
  Hex_Digit_Display hex_digit_display_4 (.value(ram_1_data[15:12]));  // open: dp
  RAM #(.addrWidth(10), .dataWidth(10), .bus("separate")) ram_2 (
    .addr(memory_mapper_1_screen_address_out), .din(memory_mapper_1_screen_value_out),
    .str(memory_mapper_1_screen_set), .clk(clock_1_out));  // open: data, sel, ld, clr
endmodule

module adder (
  input  b,
  input  a,
  input  C_in,
  output A_out,
  output C_out
);

  wire and_1_out, and_2_out, buffer_1_out, or_1_out, xor_1_out, xor_2_out;

  buf buffer_1 (buffer_1_out, C_in);
  and and_1 (and_1_out, a, b);
  xor xor_1 (xor_1_out, b, a);
  xor xor_2 (xor_2_out, xor_1_out, buffer_1_out);
  or or_1 (or_1_out, and_1_out, and_2_out);
  and and_2 (and_2_out, xor_1_out, buffer_1_out);
  buf buffer_2 (C_out, or_1_out);
  buf buffer_3 (A_out, xor_2_out);

  // Notes on the sheet:
  //   Result
endmodule

module _16_adder (
  input  [15:0] B,
  input  [15:0] A,
  output [15:0] out
);

  wire adder_1_c_out, adder_2_c_out, adder_3_c_out, adder_4_c_out, adder_5_c_out, adder_6_c_out,
       adder_7_c_out, adder_8_c_out, adder_9_c_out, adder_10_c_out, adder_11_c_out, adder_12_c_out,
       adder_13_c_out, adder_14_c_out, adder_15_c_out, adder_16_c_out;

  adder adder_1 (.b(B[15]), .a(A[15]), .C_in(adder_2_c_out), .A_out(out[15]), .C_out(adder_1_c_out));
  adder adder_2 (.b(B[14]), .a(A[14]), .C_in(adder_3_c_out), .A_out(out[14]), .C_out(adder_2_c_out));
  adder adder_3 (.b(B[13]), .a(A[13]), .C_in(adder_4_c_out), .A_out(out[13]), .C_out(adder_3_c_out));
  adder adder_4 (.b(B[12]), .a(A[12]), .C_in(adder_5_c_out), .A_out(out[12]), .C_out(adder_4_c_out));
  adder adder_5 (.b(B[11]), .a(A[11]), .C_in(adder_6_c_out), .A_out(out[11]), .C_out(adder_5_c_out));
  adder adder_6 (.b(B[10]), .a(A[10]), .C_in(adder_7_c_out), .A_out(out[10]), .C_out(adder_6_c_out));
  adder adder_7 (.b(B[9]), .a(A[9]), .C_in(adder_8_c_out), .A_out(out[9]), .C_out(adder_7_c_out));
  adder adder_8 (.b(B[8]), .a(A[8]), .C_in(adder_9_c_out), .A_out(out[8]), .C_out(adder_8_c_out));
  adder adder_9 (.b(B[7]), .a(A[7]), .C_in(adder_10_c_out), .A_out(out[7]), .C_out(adder_9_c_out));
  adder adder_10 (.b(B[6]), .a(A[6]), .C_in(adder_11_c_out), .A_out(out[6]), .C_out(adder_10_c_out));
  adder adder_11 (.b(B[5]), .a(A[5]), .C_in(adder_12_c_out), .A_out(out[5]), .C_out(adder_11_c_out));
  adder adder_12 (.b(B[4]), .a(A[4]), .C_in(adder_13_c_out), .A_out(out[4]), .C_out(adder_12_c_out));
  adder adder_13 (.b(B[3]), .a(A[3]), .C_in(adder_14_c_out), .A_out(out[3]), .C_out(adder_13_c_out));
  adder adder_14 (.b(B[2]), .a(A[2]), .C_in(adder_15_c_out), .A_out(out[2]), .C_out(adder_14_c_out));
  adder adder_15 (.b(B[1]), .a(A[1]), .C_in(adder_16_c_out), .A_out(out[1]), .C_out(adder_15_c_out));
  adder adder_16 (.b(B[0]), .a(A[0]), .C_in(1'b0), .A_out(out[0]), .C_out(adder_16_c_out));
endmodule

module _16_twos_compliment (
  input  [15:0] in_1,
  output [15:0] out_2
);

  wire [15:0] not_1_out;

  assign not_1_out = ~in_1;  // NOT_Gate not_1, 16 bits wide
  _16_adder u_16_adder_1 (.B(16'h1), .A(not_1_out), .out(out_2));
endmodule

module Processor (
  input  [15:0] RAM_in,
  input  [15:0] ROM_in,
  input  [7:0] Key_Address_In,
  input  [7:0] Keyboard_Value_In,
  input  Keyboard_Set,
  output RAM_SET,
  output RAM_GET,
  output [15:0] RAM_address,
  output [15:0] RAM_value,
  output [9:0] Screen_Address,
  output [9:0] Screen_Value,
  output [15:0] ROM_address,
  output Screen_Set,
  output ROM_enable
);

  // Buffer buffer_1 has open pins: in=ROM_in, out=open
  // Buffer buffer_2 has open pins: in=open, out=ROM_address
  // Buffer buffer_3 has open pins: in=open, out=ROM_enable
  // Buffer buffer_4 has open pins: in=RAM_in, out=open
  // Buffer buffer_5 has open pins: in=Key_Address_In, out=open
  // Buffer buffer_6 has open pins: in=open, out=RAM_address
  // Buffer buffer_7 has open pins: in=Keyboard_Value_In, out=open
  // Buffer buffer_8 has open pins: in=open, out=RAM_value
  // Buffer buffer_9 has open pins: in=open, out=RAM_SET
  // Buffer buffer_10 has open pins: in=Keyboard_Set, out=open
  // Buffer buffer_11 has open pins: in=open, out=RAM_GET
  // Buffer buffer_12 has open pins: in=open, out=Screen_Address
  // Buffer buffer_13 has open pins: in=open, out=Screen_Value
  // Buffer buffer_14 has open pins: in=open, out=Screen_Set
endmodule

module ALU (
  input  ADD,
  input  SUB,
  input  MUL,
  input  [15:0] B,
  input  [15:0] A,
  output [15:0] OUT
);

  wire [15:0] n16_adder_1_out, n16_adder_2_out, n16_multiply_1_out_3, n16_twos_compliment_1_out_2;

  _16_twos_compliment u_16_twos_compliment_1 (.in_1(B), .out_2(n16_twos_compliment_1_out_2));
  _16_adder u_16_adder_1 (.B(B), .A(A), .out(n16_adder_1_out));
  _16_adder u_16_adder_2 (.B(n16_twos_compliment_1_out_2), .A(A), .out(n16_adder_2_out));
  _16_multiply u_16_multiply_1 (.in_1(B), .in_2(A), .out_3(n16_multiply_1_out_3));
  assign OUT = ADD ? n16_adder_1_out : 16'bz;  // Controlled_Buffer controlled_buffer_1
  assign OUT = SUB ? n16_adder_2_out : 16'bz;  // Controlled_Buffer controlled_buffer_2
  assign OUT = MUL ? n16_multiply_1_out_3 : 16'bz;  // Controlled_Buffer controlled_buffer_3
endmodule

module _16_Shift_Left (
  input  [15:0] in,
  output [15:0] out
);


  assign out = {in[14:0], 1'b0};
endmodule

module _16_Shift_Right (
  input  [15:0] in,
  output [15:0] out
);


  assign out = {1'b0, in[15:1]};
endmodule

module _1_to_16_duplicator (
  input  in,
  output [15:0] out
);


  assign out = {16{in}};
endmodule

module _16_Least_Significant (
  input  [15:0] in_1,
  output out_2
);


  assign out_2 = in_1[0];
endmodule

module _16_multiply (
  input  [15:0] in_1,
  input  [15:0] in_2,
  output [15:0] out_3
);

  wire [15:0] multiplexer_1_out, multiplexer_2_out, multiplexer_3_out, multiplexer_4_out, multiplexer_5_out,
       multiplexer_6_out, multiplexer_7_out, multiplexer_8_out, multiplexer_9_out, multiplexer_10_out,
       multiplexer_11_out, multiplexer_12_out, multiplexer_13_out, multiplexer_14_out, multiplexer_15_out,
       multiplexer_16_out, n16_adder_1_out, n16_adder_2_out, n16_adder_3_out, n16_adder_4_out,
       n16_adder_5_out, n16_adder_6_out, n16_adder_7_out, n16_adder_9_out, n16_adder_10_out,
       n16_adder_11_out, n16_adder_12_out, n16_adder_13_out, n16_adder_14_out, n16_adder_15_out,
       n16_shift_left_1_out, n16_shift_left_2_out, n16_shift_left_3_out, n16_shift_left_4_out,
       n16_shift_left_5_out, n16_shift_left_6_out, n16_shift_left_7_out, n16_shift_left_8_out,
       n16_shift_left_9_out, n16_shift_left_10_out, n16_shift_left_11_out, n16_shift_left_12_out,
       n16_shift_left_13_out, n16_shift_left_14_out, n16_shift_left_15_out;

  _16_adder u_16_adder_1 (.B(multiplexer_1_out), .A(multiplexer_2_out), .out(n16_adder_1_out));
  Multiplexer #(.width(16), .enable("false")) multiplexer_1 (
    .in0({16{1'b0}}), .in1(in_1), .out(multiplexer_1_out), .sel(in_2[0]));
  _16_Shift_Left u_16_shift_left_1 (.in(in_1), .out(n16_shift_left_1_out));
  _16_adder u_16_adder_2 (.B(n16_adder_1_out), .A(n16_adder_4_out), .out(n16_adder_2_out));
  Multiplexer #(.width(16), .enable("false")) multiplexer_2 (
    .in0({16{1'b0}}), .in1(n16_shift_left_1_out), .out(multiplexer_2_out), .sel(in_2[1]));
  _16_Shift_Left u_16_shift_left_2 (.in(n16_shift_left_1_out), .out(n16_shift_left_2_out));
  _16_adder u_16_adder_3 (.B(n16_adder_2_out), .A(n16_adder_6_out), .out(n16_adder_3_out));
  _16_adder u_16_adder_4 (.B(multiplexer_3_out), .A(multiplexer_4_out), .out(n16_adder_4_out));
  Multiplexer #(.width(16), .enable("false")) multiplexer_3 (
    .in0({16{1'b0}}), .in1(n16_shift_left_2_out), .out(multiplexer_3_out), .sel(in_2[2]));
  Multiplexer #(.width(16), .enable("false")) multiplexer_4 (
    .in0({16{1'b0}}), .in1(n16_shift_left_4_out), .out(multiplexer_4_out), .sel(in_2[3]));
  _16_Shift_Left u_16_shift_left_3 (.in(n16_shift_left_4_out), .out(n16_shift_left_3_out));
  _16_Shift_Left u_16_shift_left_4 (.in(n16_shift_left_2_out), .out(n16_shift_left_4_out));
  _16_adder u_16_adder_5 (.B(multiplexer_5_out), .A(multiplexer_6_out), .out(n16_adder_5_out));
  Multiplexer #(.width(16), .enable("false")) multiplexer_5 (
    .in0({16{1'b0}}), .in1(n16_shift_left_3_out), .out(multiplexer_5_out), .sel(in_2[4]));
  _16_Shift_Left u_16_shift_left_5 (.in(n16_shift_left_3_out), .out(n16_shift_left_5_out));
  _16_adder u_16_adder_6 (.B(n16_adder_5_out), .A(n16_adder_7_out), .out(n16_adder_6_out));
  _16_adder u_16_adder_7 (.B(multiplexer_7_out), .A(multiplexer_9_out), .out(n16_adder_7_out));
  Multiplexer #(.width(16), .enable("false")) multiplexer_6 (
    .in0({16{1'b0}}), .in1(n16_shift_left_5_out), .out(multiplexer_6_out), .sel(in_2[5]));
  Multiplexer #(.width(16), .enable("false")) multiplexer_7 (
    .in0({16{1'b0}}), .in1(n16_shift_left_6_out), .out(multiplexer_7_out), .sel(in_2[6]));
  _16_Shift_Left u_16_shift_left_6 (.in(n16_shift_left_5_out), .out(n16_shift_left_6_out));
  _16_Shift_Left u_16_shift_left_7 (.in(n16_shift_left_6_out), .out(n16_shift_left_7_out));
  _16_adder u_16_adder_8 (.B(n16_adder_3_out), .A(n16_adder_11_out), .out(out_3));
  _16_adder u_16_adder_9 (.B(multiplexer_8_out), .A(multiplexer_10_out), .out(n16_adder_9_out));
  Multiplexer #(.width(16), .enable("false")) multiplexer_8 (
    .in0({16{1'b0}}), .in1(n16_shift_left_8_out), .out(multiplexer_8_out), .sel(in_2[8]));
  Multiplexer #(.width(16), .enable("false")) multiplexer_9 (
    .in0({16{1'b0}}), .in1(n16_shift_left_7_out), .out(multiplexer_9_out), .sel(in_2[7]));
  _16_Shift_Left u_16_shift_left_8 (.in(n16_shift_left_7_out), .out(n16_shift_left_8_out));
  _16_Shift_Left u_16_shift_left_9 (.in(n16_shift_left_8_out), .out(n16_shift_left_9_out));
  _16_adder u_16_adder_10 (.B(n16_adder_9_out), .A(n16_adder_12_out), .out(n16_adder_10_out));
  Multiplexer #(.width(16), .enable("false")) multiplexer_10 (
    .in0({16{1'b0}}), .in1(n16_shift_left_9_out), .out(multiplexer_10_out), .sel(in_2[9]));
  _16_Shift_Left u_16_shift_left_10 (.in(n16_shift_left_9_out), .out(n16_shift_left_10_out));
  _16_adder u_16_adder_11 (.B(n16_adder_10_out), .A(n16_adder_14_out), .out(n16_adder_11_out));
  _16_adder u_16_adder_12 (.B(multiplexer_11_out), .A(multiplexer_12_out), .out(n16_adder_12_out));
  Multiplexer #(.width(16), .enable("false")) multiplexer_11 (
    .in0({16{1'b0}}), .in1(n16_shift_left_10_out), .out(multiplexer_11_out), .sel(in_2[10]));
  Multiplexer #(.width(16), .enable("false")) multiplexer_12 (
    .in0({16{1'b0}}), .in1(n16_shift_left_11_out), .out(multiplexer_12_out), .sel(in_2[11]));
  _16_Shift_Left u_16_shift_left_11 (.in(n16_shift_left_10_out), .out(n16_shift_left_11_out));
  _16_Shift_Left u_16_shift_left_12 (.in(n16_shift_left_11_out), .out(n16_shift_left_12_out));
  _16_adder u_16_adder_13 (.B(multiplexer_13_out), .A(multiplexer_15_out), .out(n16_adder_13_out));
  Multiplexer #(.width(16), .enable("false")) multiplexer_13 (
    .in0({16{1'b0}}), .in1(n16_shift_left_12_out), .out(multiplexer_13_out), .sel(in_2[12]));
  _16_Shift_Left u_16_shift_left_13 (.in(n16_shift_left_12_out), .out(n16_shift_left_13_out));
  _16_adder u_16_adder_14 (.B(n16_adder_13_out), .A(n16_adder_15_out), .out(n16_adder_14_out));
  _16_adder u_16_adder_15 (.B(multiplexer_14_out), .A(multiplexer_16_out), .out(n16_adder_15_out));
  Multiplexer #(.width(16), .enable("false")) multiplexer_14 (
    .in0({16{1'b0}}), .in1(n16_shift_left_15_out), .out(multiplexer_14_out), .sel(in_2[14]));
  Multiplexer #(.width(16), .enable("false")) multiplexer_15 (
    .in0({16{1'b0}}), .in1(n16_shift_left_13_out), .out(multiplexer_15_out), .sel(in_2[13]));
  _16_Shift_Left u_16_shift_left_14 (.in(n16_shift_left_15_out), .out(n16_shift_left_14_out));
  _16_Shift_Left u_16_shift_left_15 (.in(n16_shift_left_13_out), .out(n16_shift_left_15_out));
  Multiplexer #(.width(16), .enable("false")) multiplexer_16 (
    .in0({16{1'b0}}), .in1(n16_shift_left_14_out), .out(multiplexer_16_out), .sel(in_2[15]));
endmodule

module Memory_Mapper (
  input  [15:0] RAM_Value_In,
  input  [15:0] RAM_Address_In,
  input  RAM_set,
  input  RAM_get,
  input  [7:0] Key_Value_In,
  input  [7:0] Key_Address_In,
  input  Key_Set,
  output RAM_set_2,
  output RAM_get_2,
  output [15:0] Ram_Value_Out,
  output [15:0] Ram_Address_Out,
  output [9:0] Screen_Value_Out,
  output [9:0] Screen_Address_Out,
  output Screen_Set
);

  wire adder_1_cout, and_1_out, and_2_out, clock_1_out, controlled_buffer_3_out, counter_1_q, Key_To_RAM_out,
       not_1_out, not_2_out, register_3_q, screen_range_1_ram_value_out;
  wire [7:0] register_1_q, register_2_q;
  wire [9:0] n16_to_10_1_out, screen_adapter_1_out;
  wire [15:0] adder_1_out, controlled_buffer_1_out, controlled_buffer_2_out, n8_to_16_1_out, n8_to_16_2_out;

  Clock clock_1 (.out(clock_1_out));
  not not_1 (not_1_out, clock_1_out);
  Multiplexer #(.width(16), .disabled(0), .enable("false")) multiplexer_1 (
    .in0(RAM_Value_In), .in1(controlled_buffer_1_out), .out(Ram_Value_Out), .sel(and_2_out));
  buf Key_To_RAM (Key_To_RAM_out, counter_1_q);
  Counter #(.width(1), .max('h1)) counter_1 (
    .count(1'b1), .Q(counter_1_q), .clk(clock_1_out));  // open: load, D, carry, clr
  not not_2 (not_2_out, counter_1_q);
  and and_1 (and_1_out, not_2_out, register_3_q);
  assign controlled_buffer_1_out = and_2_out ? n8_to_16_1_out : 16'bz;  // Controlled_Buffer controlled_buffer_1
  _8_to_16 u_8_to_16_1 (.in(register_1_q), .out(n8_to_16_1_out));
  Register register_1 (.D(Key_Value_In), .en(1'b1), .Q(register_1_q), .clk(not_1_out), .clr(and_1_out));
  Multiplexer #(.width(16), .disabled(0), .enable("false")) multiplexer_2 (
    .in0(RAM_Address_In), .in1(controlled_buffer_2_out), .out(Ram_Address_Out), .sel(and_2_out));
  Register register_2 (.D(Key_Address_In), .en(1'b1), .Q(register_2_q), .clk(not_1_out), .clr(and_1_out));
  Multiplexer #(.enable("false")) multiplexer_3 (
    .in0(RAM_set), .in1(controlled_buffer_3_out), .out(RAM_set_2), .sel(and_2_out));
  assign controlled_buffer_2_out = and_2_out ? adder_1_out : 16'bz;  // Controlled_Buffer controlled_buffer_2
  Adder #(.width(16)) adder_1 (.a(16'hfafe), .b(n8_to_16_2_out), .out(adder_1_out), .cout(adder_1_cout));  // open: cin
  _8_to_16 u_8_to_16_2 (.in(register_2_q), .out(n8_to_16_2_out));
  assign controlled_buffer_3_out = and_2_out ? register_3_q : 1'bz;  // Controlled_Buffer controlled_buffer_3
  and and_2 (and_2_out, Key_To_RAM_out, register_3_q);
  Register #(.width(1)) register_3 (.D(Key_Set), .en(1'b1), .Q(register_3_q), .clk(not_1_out), .clr(and_1_out));
  _16_to_10 u_16_to_10_1 (.in(RAM_Value_In), .out(n16_to_10_1_out));
  Screen_Adapter screen_adapter_1 (.in(RAM_Address_In), .out(screen_adapter_1_out));
  Screen_Range screen_range_1 (.Address(RAM_Address_In), .Ram_Value_Out(screen_range_1_ram_value_out));
  assign Screen_Value_Out = screen_range_1_ram_value_out ? n16_to_10_1_out : 10'bz;  // Controlled_Buffer controlled_buffer_4
  assign Screen_Address_Out = screen_range_1_ram_value_out ? screen_adapter_1_out : 10'bz;  // Controlled_Buffer controlled_buffer_5
  assign Screen_Set = screen_range_1_ram_value_out ? RAM_set : 1'bz;  // Controlled_Buffer controlled_buffer_6

  assign RAM_get_2 = RAM_get;
  // also tied to GND on the sheet: adder_1_cout

  // Notes on the sheet:
  //   NOTE: synchronize ram and screen cycle??
endmodule

module _10_to_16 (
  input  [9:0] in,
  output [15:0] out
);


  assign out = {{6{1'b0}}, in};
endmodule

module _8_to_16 (
  input  [7:0] in,
  output [15:0] out
);


  assign out = {{8{1'b0}}, in};
endmodule

module _16_to_10 (
  input  [15:0] in,
  output [9:0] out
);


  assign out = in[9:0];
endmodule

module Screen_Range (
  input  [15:0] Address,
  output Ram_Value_Out
);

  Comparator #(.width(16), .mode("unsigned")) comparator_1 (
    .a(Address), .b(16'hfbfe), .gt(Ram_Value_Out));  // open: eq, lt
endmodule

module Screen_Adapter (
  input  [15:0] in,
  output [9:0] out
);

  wire [15:0] subtractor_1_out;

  Subtractor #(.width(16)) subtractor_1 (.a(in), .b(16'hfc00), .out(subtractor_1_out));  // open: bin, bout
  _16_to_10 u_16_to_10_1 (.in(subtractor_1_out), .out(out));
endmodule
